// Logisim project sumador de 8b.circ as structural Verilog: 2 circuits, main circuit Sumador8Bits
module Sumador8Bits (
  input  in_1,
  input  in_2,
  input  Numero_A,
  input  in_4,
  input  in_5,
  input  in_6,
  input  in_7,
  input  in_8,
  input  in_9,
  input  in_10,
  input  Numero_B,
  input  in_12,
  input  in_13,
  input  in_14,
  input  in_15,
  input  in_16,
  input  C_IN,
  output out_18,
  output out_19,
  output Resultado_A_B,
  output out_21,
  output out_22,
  output out_23,
  output out_24,
  output out_25,
  output C_OUT
);

  wire sumador2bits_1_cout, sumador2bits_2_cout, sumador2bits_3_cout, sumador2bits_4_cout,
       sumador2bits_5_cout, sumador2bits_6_cout, sumador2bits_7_cout;

  Sumador2Bits sumador2bits_1 (.in_1(C_IN), .in_2(in_16), .B(in_8), .Cout(sumador2bits_1_cout), .S(out_25));
  Sumador2Bits sumador2bits_2 (
    .in_1(sumador2bits_1_cout), .in_2(in_15), .B(in_7), .Cout(sumador2bits_2_cout), .S(out_24));
  Sumador2Bits sumador2bits_3 (
    .in_1(sumador2bits_2_cout), .in_2(in_14), .B(in_6), .Cout(sumador2bits_3_cout), .S(out_23));
  Sumador2Bits sumador2bits_4 (
    .in_1(sumador2bits_3_cout), .in_2(in_13), .B(in_5), .Cout(sumador2bits_4_cout), .S(out_22));
  Sumador2Bits sumador2bits_5 (
    .in_1(sumador2bits_4_cout), .in_2(in_12), .B(in_4), .Cout(sumador2bits_5_cout), .S(out_21));
  Sumador2Bits sumador2bits_6 (
    .in_1(sumador2bits_5_cout), .in_2(Numero_B), .B(Numero_A), .Cout(sumador2bits_6_cout), .S(Resultado_A_B));
  Sumador2Bits sumador2bits_7 (
    .in_1(sumador2bits_6_cout), .in_2(in_10), .B(in_2), .Cout(sumador2bits_7_cout), .S(out_19));
  Sumador2Bits sumador2bits_8 (.in_1(sumador2bits_7_cout), .in_2(in_9), .B(in_1), .Cout(C_OUT), .S(out_18));

  // Notes on the sheet:
  //   Sumador 8 Bits
endmodule

module Sumador2Bits (
  input  in_1,
  input  in_2,
  input  B,
  output Cout,
  output S
);

  wire and_1_out, and_2_out, xor_1_out;

  xor xor_1 (xor_1_out, in_1, in_2);
  and and_1 (and_1_out, in_1, in_2);
  and and_2 (and_2_out, xor_1_out, B);
  xor xor_2 (S, xor_1_out, B);
  or or_1 (Cout, and_1_out, and_2_out);

  // Notes on the sheet:
  //   Cin
  //   A
  //   Cin + A
  //   Carry (Cin + A)
  //   Cin + A + B
  //   Carry (Cin + A + B)
endmodule
