// Logisim project FullAdder_2b_4b_8b.circ as structural Verilog: 3 circuits, main circuit Sumador8Bits
module Sumador8Bits (
  input  in_1,
  input  in_2,
  input  Numero_A,
  input  in_4,
  input  in_5,
  input  in_6,
  input  in_7,
  input  in_8,
  input  in_9,
  input  in_10,
  input  Numero_B,
  input  in_12,
  input  in_13,
  input  in_14,
  input  in_15,
  input  in_16,
  input  C_IN,
  output out_18,
  output out_19,
  output Resultado_A_B,
  output out_21,
  output out_22,
  output out_23,
  output out_24,
  output out_25,
  output C_OUT
);

  wire sumador4bits_1_cout;

  Sumador4Bits sumador4bits_1 (
    .in_2(in_5), .Numero_A(in_6), .in_4(in_7), .in_5(in_8), .Numero_B(in_13), .in_7(in_14), .in_8(in_15),
    .in_9(in_16), .Cin(C_IN), .Salida(out_22), .out_11(out_23), .out_12(out_24), .out_13(out_25),
    .Cout(sumador4bits_1_cout));
  Sumador4Bits sumador4bits_2 (
    .in_2(in_1), .Numero_A(in_2), .in_4(Numero_A), .in_5(in_4), .Numero_B(in_9), .in_7(in_10),
    .in_8(Numero_B), .in_9(in_12), .Cin(sumador4bits_1_cout), .Salida(out_18), .out_11(out_19),
    .out_12(Resultado_A_B), .out_13(out_21), .Cout(C_OUT));

  // Notes on the sheet:
  //   Full Adder 8bits
endmodule

module Sumador2Bits (
  input  in_1,
  input  in_2,
  input  B,
  output Cout,
  output S
);

  wire and_1_out, and_2_out, Cin_A_out;

  xor Cin_A (Cin_A_out, in_1, in_2);
  and and_1 (and_1_out, in_1, in_2);
  and and_2 (and_2_out, Cin_A_out, B);
  xor xor_1 (S, Cin_A_out, B);
  or or_1 (Cout, and_1_out, and_2_out);

  // Notes on the sheet:
  //   Cin
  //   A
  //   Full Adder 2bits
  //   Cin + A
  //   Carry (Cin + A)
  //   Cin + A + B
  //   Carry (Cin + A + B)
endmodule

module Sumador4Bits (
  input  Cin,
  input  in_2,
  input  Numero_A,
  input  in_4,
  input  in_5,
  input  Numero_B,
  input  in_7,
  input  in_8,
  input  in_9,
  output Salida,
  output out_11,
  output out_12,
  output out_13,
  output Cout
);

  wire sumador2bits_1_cout, sumador2bits_2_cout, sumador2bits_3_cout;

  Sumador2Bits sumador2bits_1 (.in_1(Cin), .in_2(in_9), .B(in_5), .Cout(sumador2bits_1_cout), .S(out_13));
  Sumador2Bits sumador2bits_2 (
    .in_1(sumador2bits_1_cout), .in_2(in_8), .B(in_4), .Cout(sumador2bits_2_cout), .S(out_12));
  Sumador2Bits sumador2bits_3 (
    .in_1(sumador2bits_2_cout), .in_2(in_7), .B(Numero_A), .Cout(sumador2bits_3_cout), .S(out_11));
  Sumador2Bits sumador2bits_4 (.in_1(sumador2bits_3_cout), .in_2(Numero_B), .B(in_2), .Cout(Cout), .S(Salida));

  // Notes on the sheet:
  //   Full Adder 4bits
endmodule
